// Logisim project pipelinelogisim.circ as structural Verilog: 17 circuits, main circuit Processor
module Processor (
  input  Reset,
  input  [3:0] Display_Address
);

  wire alu_1_is, alu_1_is_2, Clock, conflicted_data_1_out_5, flags_1_flags_e, flags_1_flags_gt, isBeq,
       isBeq_EX, isBeq_MA, isBeq_RW, isBgt, isBgt_EX, isBgt_MA, isBgt_RW, isBranchTaken, isCall, isCall_EX,
       isCall_MA, isCall_RW, isImme, isLd, isLd_EX, isLd_MA, isLd_RW, isRet, isRet_EX, isRet_MA, isRet_RW,
       isSt, isSt_EX, isSt_MA, isSt_RW, isUBranch, isUBranch_EX, isUBranch_MA, isUBranch_RW, isWb, isWb_EX,
       isWb_MA, isWb_RW, lock_branch_1_bubble, RW__EX_op2, RW__MA_op2, RW__OF_op1, RW__OF_op2, stall;
  wire [1:0] RWMA__EX_op1, RWMA__EX_op2;
  wire [3:0] multiplexer_7_out, multiplexer_9_out, multiplexer_13_out, register_file_1_displayd_2,
       register_file_1_displayd_3;
  wire [12:0] ALUsignals, ALUsignals_EX;
  wire [23:0] register_file_1_displayd;
  wire [31:0] A, A_o, adder_1_out, adder_2_out, aluResult, aluResult_o, aluResult_o2, B, B_o,
       bit_extender_1_out, branchPC, branchTarget, branchTarget_o, calculate_immediate_1_immx, data,
       Inst_out, Inst_out2, Inst_out3, Inst_out4, Instruction, ldResult, ldResult_o, multiplexer_1_out,
       multiplexer_2_out, multiplexer_4_out, multiplexer_8_out, multiplexer_11_out, op2, op2_1, op2_2, PC,
       PC_out1, PC_out2, PC_out3, PC_out4, register_file_1_readd1, register_file_1_readd2, shifter_1_out;

  Register #(.width(32)) u_PC (.D(multiplexer_2_out), .en(stall), .Q(PC), .clk(Clock), .clr(Reset));
  Multiplexer #(.select(2), .width(32), .enable("false")) multiplexer_1 (
    .in0(B_o), .in1(data), .in2(aluResult_o), .in3(aluResult_o), .out(multiplexer_1_out), .sel(RWMA__EX_op2));
  Multiplexer #(.width(32), .enable("false")) multiplexer_2 (
    .in0(adder_1_out), .in1(branchPC), .out(multiplexer_2_out), .sel(isBranchTaken));
  assign bit_extender_1_out = {{5{Inst_out[26]}}, Inst_out[26:0]};  // Bit_Extender bit_extender_1
  Multiplexer #(.width(32), .enable("false")) multiplexer_3 (
    .in0(branchTarget_o), .in1(multiplexer_4_out), .out(branchPC), .sel(isRet_EX));
  ALU alu_1 (
    .A(multiplexer_4_out), .B(multiplexer_1_out), .ALUsignals(ALUsignals_EX), .aluResult(aluResult),
    .is(alu_1_is), .is_2(alu_1_is_2));
  Adder #(.width(32)) adder_1 (.a(32'h4), .b(PC), .out(adder_1_out));  // open: cin, cout
  Shifter #(.width(32)) shifter_1 (.in(bit_extender_1_out), .\dist (5'b00010), .out(shifter_1_out));
  Adder #(.width(32)) adder_2 (.a(PC_out4), .b(32'h4), .out(adder_2_out));  // open: cin, cout
  Calculate_Immediate calculate_immediate_1 (.imm(Inst_out[17:0]), .immx(calculate_immediate_1_immx));
  Adder #(.width(32)) adder_3 (.a(shifter_1_out), .b(PC_out1), .out(branchTarget));  // open: cin, cout
  Multiplexer #(.select(2), .width(32), .enable("false")) multiplexer_4 (
    .in0(A_o), .in1(data), .in2(aluResult_o), .in3(aluResult_o), .out(multiplexer_4_out), .sel(RWMA__EX_op1));
  Flags flags_1 (
    .isCmp(ALUsignals_EX[0]), .is(alu_1_is), .is_2(alu_1_is_2), .flags_GT(flags_1_flags_gt),
    .flags_E(flags_1_flags_e));
  Multiplexer #(.select(2), .width(32), .enable("false")) multiplexer_5 (
    .in0(aluResult_o2), .in1(ldResult_o), .in2(adder_2_out), .out(data), .sel({isCall_RW, isLd_RW}));  // open: in3
  conflicted_data conflicted_data_1 (
    .OF(Inst_out), .EX(Inst_out2), .MA(Inst_out3), .RW(Inst_out4), .out_5(conflicted_data_1_out_5));
  Clock u_Clock (.out(Clock));
  ROM #(.addrWidth(24), .dataWidth(32)) rom_1 (.addr(PC[25:2]), .data(Instruction));  // open: sel
  Multiplexer #(.width(32), .enable("false")) multiplexer_6 (
    .in0(op2), .in1(calculate_immediate_1_immx), .out(B), .sel(isImme));
  Memory_Unit memory_unit_1 (
    .MAR(aluResult_o), .ldResult(ldResult), .MDR(multiplexer_11_out), .isSt(isSt_MA), .isLd(isLd_MA),
    .Clock(Clock), .Reset(Reset));
  not not_1 (stall, conflicted_data_1_out_5);
  Hex_Digit_Display hex_digit_display_1 (.value(register_file_1_displayd_3));  // open: dp
  Multiplexer #(.width(4), .enable("false")) multiplexer_7 (
    .in0(Inst_out[17:14]), .in1(Inst_out[25:22]), .out(multiplexer_7_out), .sel(isSt));
  Branch_Unit branch_unit_1 (
    .isBeq(isBeq_EX), .isUBranch(isUBranch_EX), .flags_E(flags_1_flags_e), .isBgt(isBgt_EX),
    .flags_GT(flags_1_flags_gt), .isBranchTaken(isBranchTaken));
  Multiplexer #(.width(32), .enable("false")) multiplexer_8 (
    .in0(op2_1), .in1(data), .out(multiplexer_8_out), .sel(RW__EX_op2));
  Hex_Digit_Display hex_digit_display_2 (.value(register_file_1_displayd_2));  // open: dp
  Multiplexer #(.width(4), .enable("false")) multiplexer_9 (
    .in0(Inst_out[21:18]), .in1(4'b1111), .out(multiplexer_9_out), .sel(isRet));
  Register_File register_file_1 (
    .ReadA1(multiplexer_9_out), .ReadA2(multiplexer_7_out), .WriteE(isWb_RW), .WriteD(data),
    .ReadD1(register_file_1_readd1), .ReadD2(register_file_1_readd2), .Clock(Clock), .Reset(Reset),
    .DisplayD({register_file_1_displayd_3, register_file_1_displayd_2, register_file_1_displayd}),
    .DisplayA(Display_Address), .WriteA(multiplexer_13_out));
  Multiplexer #(.width(32), .enable("false")) multiplexer_10 (
    .in0(register_file_1_readd2), .in1(data), .out(op2), .sel(RW__OF_op2));
  Multiplexer #(.width(32), .enable("false")) multiplexer_11 (
    .in0(op2_2), .in1(data), .out(multiplexer_11_out), .sel(RW__MA_op2));
  Hex_Digit_Display hex_digit_display_3 (.value(register_file_1_displayd[23:20]));  // open: dp
  Multiplexer #(.width(32), .enable("false")) multiplexer_12 (
    .in0(register_file_1_readd1), .in1(data), .out(A), .sel(RW__OF_op1));
  forwarding forwarding_1 (
    .MA_RW(Inst_out4), .EX_MA(Inst_out3), .OF_EX(Inst_out2), .IF_OF(Inst_out), .RW__MA_op2(RW__MA_op2),
    .RWMA__EX_op2(RWMA__EX_op2), .RW__EX_op2(RW__EX_op2), .RWMA__EX_op1(RWMA__EX_op1),
    .RW__OF_op2(RW__OF_op2), .RW__OF_op1(RW__OF_op1));
  Hex_Digit_Display hex_digit_display_4 (.value(register_file_1_displayd[19:16]));  // open: dp
  Hex_Digit_Display hex_digit_display_5 (.value(register_file_1_displayd[15:12]));  // open: dp
  Control_Unit control_unit_1 (
    .isSt(isSt), .isLd(isLd), .isBeq(isBeq), .isBgt(isBgt), .isRet(isRet), .I_bit(Inst_out[26]),
    .isImmediate(isImme), .opcode(Inst_out[31:27]), .isWb(isWb), .isUbranch(isUBranch), .isCall(isCall),
    .ALUsignals(ALUsignals));
  EX_MA ex_ma_1 (
    .clock(Clock), .clear(Reset), .isWb_2(isWb_MA), .isUBranch_2(isUBranch_MA), .isCall_2(isCall_MA),
    .isST_2(isSt_MA), .isLd_2(isLd_MA), .isBeq_2(isBeq_MA), .isBgt_2(isBgt_MA), .isRet_2(isRet_MA),
    .Instruction_2(Inst_out3), .PC_input_2(PC_out3), .aluResult_2(aluResult_o), .op2_input_2(op2_2),
    .PC_input(PC_out2), .aluResult(aluResult), .op2_input(multiplexer_8_out), .Instruction(Inst_out2),
    .isSt(isSt_EX), .isLd(isLd_EX), .isBeq(isBeq_EX), .isBgt(isBgt_EX), .isRet(isRet_EX), .isWb(isWb_EX),
    .isUBranch(isUBranch_EX), .isCall(isCall_EX));
  Hex_Digit_Display hex_digit_display_6 (.value(register_file_1_displayd[11:8]));  // open: dp
  Hex_Digit_Display hex_digit_display_7 (.value(register_file_1_displayd[7:4]));  // open: dp
  Multiplexer #(.width(4), .enable("false")) multiplexer_13 (
    .in0(Inst_out4[25:22]), .in1(4'b1111), .out(multiplexer_13_out), .sel(isCall_RW));
  Hex_Digit_Display hex_digit_display_8 (.value(register_file_1_displayd[3:0]));  // open: dp
  lock_branch lock_branch_1 (.isBranchTaken(isBranchTaken), .stall(stall), .bubble(lock_branch_1_bubble));
  MA_RW ma_rw_1 (
    .pc_input(PC_out3), .ldResult(ldResult), .aluResult(aluResult_o), .instruction(Inst_out3), .clock(Clock),
    .clear(Reset), .pc_o_p(PC_out4), .IdResult_o_p(ldResult_o), .aluResult_o_p(aluResult_o2),
    .ins_o_p(Inst_out4), .isSt(isSt_MA), .isLd(isLd_MA), .isBeq(isBeq_MA), .isBgt(isBgt_MA),
    .isRet(isRet_MA), .isWb(isWb_MA), .isUBranch(isUBranch_MA), .isCall(isCall_MA),
    .isUBranch_2(isUBranch_RW), .isCall_2(isCall_RW), .isWb_2(isWb_RW), .isBeq_2(isBeq_RW),
    .isBgt_2(isBgt_RW), .isRet_2(isRet_RW), .isSt_2(isSt_RW), .isLd_2(isLd_RW));
  IF_OF if_of_1 (
    .Instruction(Instruction), .Instruction_O_P(Inst_out), .PC(PC), .O_P_of_PC(PC_out1), .clear(Reset),
    .clock(Clock), .isBranchTaken(isBranchTaken), .stall(stall));
  OF_EX of_ex_1 (
    .PC(PC_out1), .PC_2(PC_out2), .Instruction(Inst_out), .Instruction_2(Inst_out2),
    .Bubble(lock_branch_1_bubble), .BranchTarget(branchTarget), .BranchTarget_2(branchTarget_o), .A_2(A_o),
    .A(A), .B_2(B_o), .B(B), .OP2(op2), .OP2_2(op2_1), .isSt(isSt), .isSt_2(isSt_EX), .isLd(isLd),
    .isLd_2(isLd_EX), .isBeq(isBeq), .isBeq_2(isBeq_EX), .isBgt(isBgt), .isBgt_2(isBgt_EX), .isRet(isRet),
    .isRet_2(isRet_EX), .isUbranch(isUBranch), .isUbranch_2(isUBranch_EX), .isWb(isWb), .isWb_2(isWb_EX),
    .isCall(isCall), .isCall_2(isCall_EX), .Alusignals(ALUsignals), .Alusignals_2(ALUsignals_EX),
    .reset(Reset), .clock(Clock));

  // Notes on the sheet:
  //   ALUsignals
  //   branch PC
  //   B
  //   isBranchTaken
  //   A
  //   ALU
  //   aluResult
  //   pc
  //   pc+4
  //   branchPC
  //   offset
  //   pc
  //   isRet
  //   is>
  //   is=
  //   MAR
  //   calc immx
  //   imm
  //   branchTarget
  //   Flags
  //   isCmp
  //   MDR
  //   Memory
  //   Unit
  //   ldResult
  //   data
  //   FULLY PIPELINED PROCESSOR
  //   Instruction Memory
  //   contents of rom_1 (hex, n*v repeats v):
  //   4c400009 4c800006 4cc00000 7c4c0004 758c0004 7c8c0008 760c0008 e18000 90000000
  //   immx
  //   flags(GT)
  //   flags(E)
  //   isLd
  //   isSt
  //   isLd
  //   isCall
  //   instruction
  //   rs2
  //   rd
  //   isSt
  //   op2
  //   isImmediate
  //   isBranchTaken
  //   Branch
  //   Unit
  //   rs1
  //   E
  //   Register
  //   A
  //   File
  //   D
  //   op1
  //   isBeq
  //   isBgt
  //   isUBranch
  //   isRet
  //   isWb
  //   address
  //   data
  //   Display Register
  //   opcode
  //   CONTROL
  //   I bit
  //   UNIT
  //   isCall
  //   rd
endmodule

module Control_Unit (
  input  I_bit,
  input  [4:0] opcode,
  output isSt,
  output isLd,
  output isBeq,
  output isBgt,
  output isRet,
  output isImmediate,
  output isWb,
  output isUbranch,
  output isCall,
  output [12:0] ALUsignals
);

  wire and_6_out, and_7_out, and_8_out, and_9_out, and_10_out, and_12_out, and_13_out, nand_1_out;

  nand nand_1 (nand_1_out, opcode[0], opcode[1]);
  and and_1 (isSt, opcode[0], opcode[1], opcode[2], opcode[3], ~opcode[4]);  // AND_Gate
  and and_2 (isLd, ~opcode[0], opcode[1], opcode[2], opcode[3], ~opcode[4]);  // AND_Gate
  and and_3 (isBeq, ~opcode[0], ~opcode[1], ~opcode[2], ~opcode[3], opcode[4]);  // AND_Gate
  and and_4 (isBgt, opcode[0], ~opcode[1], ~opcode[2], ~opcode[3], opcode[4]);  // AND_Gate
  and and_5 (isRet, ~opcode[0], ~opcode[1], opcode[2], ~opcode[3], opcode[4]);  // AND_Gate
  and and_6 (and_6_out, opcode[0], ~opcode[1], opcode[2], ~opcode[4]);  // AND_Gate
  and and_7 (and_7_out, opcode[0], opcode[2], opcode[3], ~opcode[4]);  // AND_Gate
  and and_8 (and_8_out, opcode[4], nand_1_out);
  and and_9 (and_9_out, opcode[1], ~opcode[2], ~opcode[3], opcode[4]);  // AND_Gate
  and and_10 (and_10_out, ~opcode[0], ~opcode[1], opcode[2], ~opcode[3], opcode[4]);  // AND_Gate
  and and_11 (isCall, opcode[0], opcode[1], ~opcode[2], ~opcode[3], opcode[4]);  // AND_Gate
  and and_12 (and_12_out, ~opcode[0], ~opcode[1], ~opcode[2], ~opcode[3], ~opcode[4]);  // AND_Gate
  and and_13 (and_13_out, opcode[1], opcode[2], opcode[3], ~opcode[4]);  // AND_Gate
  and isSub (ALUsignals[2], opcode[0], ~opcode[1], ~opcode[2], ~opcode[3], ~opcode[4]);  // AND_Gate
  and isCmp (ALUsignals[0], opcode[0], ~opcode[1], opcode[2], ~opcode[3], ~opcode[4]);  // AND_Gate
  and isMul (ALUsignals[3], ~opcode[0], opcode[1], ~opcode[2], ~opcode[3], ~opcode[4]);  // AND_Gate
  and isDiv (ALUsignals[4], opcode[0], opcode[1], ~opcode[2], ~opcode[3], ~opcode[4]);  // AND_Gate
  and isMod (ALUsignals[5], ~opcode[0], ~opcode[1], opcode[2], ~opcode[3], ~opcode[4]);  // AND_Gate
  and isLsl (ALUsignals[7], ~opcode[0], opcode[1], ~opcode[2], opcode[3], ~opcode[4]);  // AND_Gate
  and isLsr (ALUsignals[8], opcode[0], opcode[1], ~opcode[2], opcode[3], ~opcode[4]);  // AND_Gate
  and isAsr (ALUsignals[9], ~opcode[0], ~opcode[1], opcode[2], opcode[3], ~opcode[4]);  // AND_Gate
  and isOr (ALUsignals[12], opcode[0], opcode[1], opcode[2], ~opcode[3], ~opcode[4]);  // AND_Gate
  and isAnd (ALUsignals[11], ~opcode[0], opcode[1], opcode[2], ~opcode[3], ~opcode[4]);  // AND_Gate
  and isNot (ALUsignals[10], ~opcode[0], ~opcode[1], ~opcode[2], opcode[3], ~opcode[4]);  // AND_Gate
  and isMov (ALUsignals[6], opcode[0], ~opcode[1], ~opcode[2], opcode[3], ~opcode[4]);  // AND_Gate
  or or_1 (isUbranch, and_9_out, and_10_out);
  or isAdd (ALUsignals[1], and_12_out, and_13_out);
  nor nor_1 (isWb, and_6_out, and_7_out, and_8_out);

  assign isImmediate = I_bit;

  // Notes on the sheet:
  //   op1
  //   op2
  //   op3
  //   op4
  //   op5
endmodule

module Register_File (
  input  Clock,
  input  Reset,
  input  [31:0] WriteD,
  input  [3:0] ReadA1,
  input  WriteE,
  input  [3:0] WriteA,
  input  [3:0] ReadA2,
  input  [3:0] DisplayA,
  output [31:0] ReadD1,
  output [31:0] ReadD2,
  output [31:0] DisplayD
);

  wire demultiplexer_1_out0, demultiplexer_1_out1, demultiplexer_1_out2, demultiplexer_1_out3,
       demultiplexer_1_out4, demultiplexer_1_out5, demultiplexer_1_out6, demultiplexer_1_out7,
       demultiplexer_1_out8, demultiplexer_1_out9, demultiplexer_1_out10, demultiplexer_1_out11,
       demultiplexer_1_out12, demultiplexer_1_out13, demultiplexer_1_out14, demultiplexer_1_out15,
       multiplexer_2_out, or_1_out, or_2_out;
  wire [31:0] multiplexer_1_out, r0_q, r1_q, r2_q, r3_q, r4_q, r5_q, r6_q, r7_q, r8_q, r9_q, r10_q, r11_q,
       r12_q, r13_q, r14_q, r15_q;

  Demultiplexer #(.select(4), .disabled(0), .enable("false")) demultiplexer_1 (
    .out0(demultiplexer_1_out0), .out1(demultiplexer_1_out1), .out2(demultiplexer_1_out2),
    .out3(demultiplexer_1_out3), .out4(demultiplexer_1_out4), .out5(demultiplexer_1_out5),
    .out6(demultiplexer_1_out6), .out7(demultiplexer_1_out7), .out8(demultiplexer_1_out8),
    .out9(demultiplexer_1_out9), .out10(demultiplexer_1_out10), .out11(demultiplexer_1_out11),
    .out12(demultiplexer_1_out12), .out13(demultiplexer_1_out13), .out14(demultiplexer_1_out14),
    .out15(demultiplexer_1_out15), .in(WriteE), .sel(WriteA));
  Multiplexer #(.width(32), .enable("false")) multiplexer_1 (
    .in0(WriteD), .in1(32'h3fffffc), .out(multiplexer_1_out), .sel(Reset));
  or or_1 (or_1_out, demultiplexer_1_out14, Reset);
  Multiplexer #(.enable("false")) multiplexer_2 (.in0(or_2_out), .out(multiplexer_2_out), .sel(1'b0));  // open: in1
  or or_2 (or_2_out, Clock, Reset);
  Register #(.width(32)) r0 (.D(WriteD), .en(demultiplexer_1_out0), .Q(r0_q), .clk(Clock), .clr(Reset));
  Register #(.width(32)) r1 (.D(WriteD), .en(demultiplexer_1_out1), .Q(r1_q), .clk(Clock), .clr(Reset));
  Register #(.width(32)) r2 (.D(WriteD), .en(demultiplexer_1_out2), .Q(r2_q), .clk(Clock), .clr(Reset));
  Register #(.width(32)) r3 (.D(WriteD), .en(demultiplexer_1_out3), .Q(r3_q), .clk(Clock), .clr(Reset));
  Register #(.width(32)) r4 (.D(WriteD), .en(demultiplexer_1_out4), .Q(r4_q), .clk(Clock), .clr(Reset));
  Register #(.width(32)) r5 (.D(WriteD), .en(demultiplexer_1_out5), .Q(r5_q), .clk(Clock), .clr(Reset));
  Register #(.width(32)) r6 (.D(WriteD), .en(demultiplexer_1_out6), .Q(r6_q), .clk(Clock), .clr(Reset));
  Register #(.width(32)) r7 (.D(WriteD), .en(demultiplexer_1_out7), .Q(r7_q), .clk(Clock), .clr(Reset));
  Register #(.width(32)) r8 (.D(WriteD), .en(demultiplexer_1_out8), .Q(r8_q), .clk(Clock), .clr(Reset));
  Register #(.width(32)) r9 (.D(WriteD), .en(demultiplexer_1_out9), .Q(r9_q), .clk(Clock), .clr(Reset));
  Register #(.width(32)) r10 (.D(WriteD), .en(demultiplexer_1_out10), .Q(r10_q), .clk(Clock), .clr(Reset));
  Register #(.width(32)) r11 (.D(WriteD), .en(demultiplexer_1_out11), .Q(r11_q), .clk(Clock), .clr(Reset));
  Register #(.width(32)) r12 (.D(WriteD), .en(demultiplexer_1_out12), .Q(r12_q), .clk(Clock), .clr(Reset));
  Register #(.width(32)) r13 (.D(WriteD), .en(demultiplexer_1_out13), .Q(r13_q), .clk(Clock), .clr(Reset));
  Register #(.width(32)) r14 (.D(multiplexer_1_out), .en(or_1_out), .Q(r14_q), .clk(multiplexer_2_out));  // open: clr
  Register #(.width(32)) r15 (.D(WriteD), .en(demultiplexer_1_out15), .Q(r15_q), .clk(Clock), .clr(Reset));
  Multiplexer #(.select(4), .width(32), .disabled(0), .enable("false")) multiplexer_3 (
    .in0(r0_q), .in1(r1_q), .in2(r2_q), .in3(r3_q), .in4(r4_q), .in5(r5_q), .in6(r6_q), .in7(r7_q),
    .in8(r8_q), .in9(r9_q), .in10(r10_q), .in11(r11_q), .in12(r12_q), .in13(r13_q), .in14(r14_q),
    .in15(r15_q), .out(ReadD1), .sel(ReadA1));
  Multiplexer #(.select(4), .width(32), .disabled(0), .enable("false")) multiplexer_4 (
    .in0(r0_q), .in1(r1_q), .in2(r2_q), .in3(r3_q), .in4(r4_q), .in5(r5_q), .in6(r6_q), .in7(r7_q),
    .in8(r8_q), .in9(r9_q), .in10(r10_q), .in11(r11_q), .in12(r12_q), .in13(r13_q), .in14(r14_q),
    .in15(r15_q), .out(ReadD2), .sel(ReadA2));
  Multiplexer #(.select(4), .width(32), .disabled(0), .enable("false")) multiplexer_5 (
    .in0(r0_q), .in1(r1_q), .in2(r2_q), .in3(r3_q), .in4(r4_q), .in5(r5_q), .in6(r6_q), .in7(r7_q),
    .in8(r8_q), .in9(r9_q), .in10(r10_q), .in11(r11_q), .in12(r12_q), .in13(r13_q), .in14(r14_q),
    .in15(r15_q), .out(DisplayD), .sel(DisplayA));
endmodule

module ALU (
  input  [31:0] A,
  input  [31:0] B,
  input  [12:0] ALUsignals,
  output [31:0] aluResult,
  output is,
  output is_2
);

  wire [31:0] adder_1_out, and_1_out, divider_1_out, divider_1_rem, multiplier_1_out, not_1_out, or_1_out,
       shifter_1_out, shifter_2_out, shifter_3_out, subtractor_1_out;

  Adder #(.width(32)) adder_1 (.a(A), .b(B), .out(adder_1_out));  // open: cin, cout
  Subtractor #(.width(32)) subtractor_1 (.a(A), .b(B), .out(subtractor_1_out));  // open: bin, bout
  Multiplier #(.width(32)) multiplier_1 (.a(A), .b(B), .out(multiplier_1_out));  // open: cin, cout
  Divider #(.width(32)) divider_1 (.a(A), .b(B), .out(divider_1_out), .rem(divider_1_rem));  // open: upper
  Comparator #(.width(32)) comparator_1 (.a(A), .b(B), .gt(is), .eq(is_2));  // open: lt
  Shifter #(.width(32)) shifter_1 (.in(A), .\dist (B[4:0]), .out(shifter_1_out));
  Shifter #(.width(32), .shift("lr")) shifter_2 (.in(A), .\dist (B[4:0]), .out(shifter_2_out));
  Shifter #(.width(32), .shift("ar")) shifter_3 (.in(A), .\dist (B[4:0]), .out(shifter_3_out));
  assign not_1_out = ~B;  // NOT_Gate not_1, 32 bits wide
  assign and_1_out = A & B;  // AND_Gate and_1, 32 bits wide
  assign or_1_out = A | B;  // OR_Gate or_1, 32 bits wide
  assign aluResult = ALUsignals[1] ? adder_1_out : 32'bz;  // Controlled_Buffer controlled_buffer_1
  assign aluResult = ALUsignals[2] ? subtractor_1_out : 32'bz;  // Controlled_Buffer controlled_buffer_2
  assign aluResult = ALUsignals[3] ? multiplier_1_out : 32'bz;  // Controlled_Buffer controlled_buffer_3
  assign aluResult = ALUsignals[4] ? divider_1_out : 32'bz;  // Controlled_Buffer controlled_buffer_4
  assign aluResult = ALUsignals[5] ? divider_1_rem : 32'bz;  // Controlled_Buffer controlled_buffer_5
  assign aluResult = ALUsignals[6] ? B : 32'bz;  // Controlled_Buffer controlled_buffer_6
  assign aluResult = ALUsignals[7] ? shifter_1_out : 32'bz;  // Controlled_Buffer controlled_buffer_7
  assign aluResult = ALUsignals[8] ? shifter_2_out : 32'bz;  // Controlled_Buffer controlled_buffer_8
  assign aluResult = ALUsignals[9] ? shifter_3_out : 32'bz;  // Controlled_Buffer controlled_buffer_9
  assign aluResult = ALUsignals[10] ? not_1_out : 32'bz;  // Controlled_Buffer controlled_buffer_10
  assign aluResult = ALUsignals[11] ? and_1_out : 32'bz;  // Controlled_Buffer controlled_buffer_11
  assign aluResult = ALUsignals[12] ? or_1_out : 32'bz;  // Controlled_Buffer controlled_buffer_12

  // Notes on the sheet:
  //   add
  //   sub
  //   mul
  //   div
  //   cmp
  //   lsr
  //   mod
  //   lsl
  //   asr
endmodule

module Flags (
  input  isCmp,
  input  is,
  input  is_2,
  output flags_GT,
  output flags_E
);

  D_Flip_Flop #(.trigger("high")) d_ff_1 (.clk(isCmp), .D(is), .Q(flags_GT));  // open: Qn, preset, en, reset
  D_Flip_Flop #(.trigger("high")) d_ff_2 (.clk(isCmp), .D(is_2), .Q(flags_E));  // open: Qn, preset, en, reset
endmodule

module Branch_Unit (
  input  isUBranch,
  input  isBeq,
  input  flags_E,
  input  isBgt,
  input  flags_GT,
  output isBranchTaken
);

  wire and_1_out, and_2_out;

  and and_1 (and_1_out, isBeq, flags_E);
  and and_2 (and_2_out, isBgt, flags_GT);
  or or_1 (isBranchTaken, isUBranch, and_1_out, and_2_out);
endmodule

module Memory_Unit (
  input  [31:0] MAR,
  input  isLd,
  input  [31:0] MDR,
  input  isSt,
  input  Clock,
  input  Reset,
  output [31:0] ldResult
);

  RAM #(.addrWidth(24), .dataWidth(32), .bus("separate")) ram_1 (
    .addr(MAR[25:2]), .din(MDR), .data(ldResult), .str(isSt), .clk(Clock), .ld(isLd), .clr(Reset));  // open: sel
endmodule

module Calculate_Immediate (
  input  [17:0] imm,
  output [31:0] immx
);

  wire [31:0] bit_extender_1_out, bit_extender_2_out, shifter_1_out;

  assign bit_extender_1_out = {{16{1'b0}}, imm[15:0]};  // Bit_Extender bit_extender_1
  assign bit_extender_2_out = {{16{imm[15]}}, imm[15:0]};  // Bit_Extender bit_extender_2
  Shifter #(.width(32)) shifter_1 (.in(bit_extender_1_out), .\dist (5'b10000), .out(shifter_1_out));
  Multiplexer #(.select(2), .width(32), .enable("false")) multiplexer_1 (
    .in0(bit_extender_2_out), .in1(bit_extender_1_out), .in2(shifter_1_out), .out(immx), .sel(imm[17:16]));  // open: in3

  // Notes on the sheet:
  //   modifier bits
  //   high
  //   default
  //   unsigned
endmodule

// IF-OF LATCH
module IF_OF (
  input  [31:0] PC,
  input  [31:0] Instruction,
  input  isBranchTaken,
  input  clear,
  input  clock,
  input  stall,
  output [31:0] O_P_of_PC,
  output [31:0] Instruction_O_P
);

  wire [31:0] multiplexer_1_out;

  Register #(.width(32)) register_1 (.D(PC), .en(stall), .Q(O_P_of_PC), .clk(clock), .clr(clear));
  Register #(.width(32)) register_2 (.D(multiplexer_1_out), .en(stall), .Q(Instruction_O_P), .clk(clock), .clr(clear));
  Multiplexer #(.width(32), .enable("false")) multiplexer_1 (
    .in0(Instruction), .in1(32'h68000000), .out(multiplexer_1_out), .sel(isBranchTaken));
endmodule

// OF-EX LATCH
module OF_EX (
  input  [31:0] PC,
  input  [31:0] Instruction,
  input  Bubble,
  input  [31:0] BranchTarget,
  input  [31:0] A,
  input  [31:0] B,
  input  [31:0] OP2,
  input  isSt,
  input  isLd,
  input  isBeq,
  input  isBgt,
  input  isRet,
  input  isUbranch,
  input  isWb,
  input  isCall,
  input  [12:0] Alusignals,
  input  clock,
  input  reset,
  output [31:0] PC_2,
  output [31:0] Instruction_2,
  output [31:0] BranchTarget_2,
  output [31:0] A_2,
  output [31:0] B_2,
  output [31:0] OP2_2,
  output isSt_2,
  output isLd_2,
  output isBeq_2,
  output isBgt_2,
  output isRet_2,
  output isUbranch_2,
  output isWb_2,
  output isCall_2,
  output [12:0] Alusignals_2
);

  wire multiplexer_1_out, multiplexer_3_out, multiplexer_4_out, multiplexer_5_out, multiplexer_6_out,
       multiplexer_7_out, multiplexer_9_out, multiplexer_10_out;
  wire [12:0] multiplexer_8_out;
  wire [31:0] multiplexer_2_out;

  Multiplexer #(.enable("false")) multiplexer_1 (.in0(isCall), .in1(1'b0), .out(multiplexer_1_out), .sel(Bubble));
  Multiplexer #(.width(32), .enable("false")) multiplexer_2 (
    .in0(Instruction), .in1(32'h68000000), .out(multiplexer_2_out), .sel(Bubble));
  Multiplexer #(.enable("false")) multiplexer_3 (.in0(isBeq), .in1(1'b0), .out(multiplexer_3_out), .sel(Bubble));
  Multiplexer #(.enable("false")) multiplexer_4 (.in0(isBgt), .in1(1'b0), .out(multiplexer_4_out), .sel(Bubble));
  Multiplexer #(.enable("false")) multiplexer_5 (.in0(isRet), .in1(1'b0), .out(multiplexer_5_out), .sel(Bubble));
  Multiplexer #(.enable("false")) multiplexer_6 (.in0(isUbranch), .in1(1'b0), .out(multiplexer_6_out), .sel(Bubble));
  Multiplexer #(.enable("false")) multiplexer_7 (.in0(isWb), .in1(1'b0), .out(multiplexer_7_out), .sel(Bubble));
  Multiplexer #(.width(13), .enable("false")) multiplexer_8 (
    .in0(Alusignals), .in1({13{1'b0}}), .out(multiplexer_8_out), .sel(Bubble));
  Register #(.width(32)) register_1 (.D(PC), .en(1'b1), .Q(PC_2), .clk(clock), .clr(reset));
  Register #(.width(32)) register_2 (.D(multiplexer_2_out), .en(1'b1), .Q(Instruction_2), .clk(clock), .clr(reset));
  Register #(.width(32)) register_3 (.D(BranchTarget), .en(1'b1), .Q(BranchTarget_2), .clk(clock), .clr(reset));
  Register #(.width(32)) register_4 (.D(A), .en(1'b1), .Q(A_2), .clk(clock), .clr(reset));
  Register #(.width(32)) register_5 (.D(B), .en(1'b1), .Q(B_2), .clk(clock), .clr(reset));
  Register #(.width(32)) register_6 (.D(OP2), .en(1'b1), .Q(OP2_2), .clk(clock), .clr(reset));
  Multiplexer #(.enable("false")) multiplexer_9 (.in0(isSt), .in1(1'b0), .out(multiplexer_9_out), .sel(Bubble));
  Register #(.width(1)) register_7 (.D(multiplexer_9_out), .en(1'b1), .Q(isSt_2), .clk(clock), .clr(reset));
  Multiplexer #(.enable("false")) multiplexer_10 (.in0(isLd), .in1(1'b0), .out(multiplexer_10_out), .sel(Bubble));
  Register #(.width(1)) register_8 (.D(multiplexer_4_out), .en(1'b1), .Q(isBgt_2), .clk(clock), .clr(reset));
  Register #(.width(1)) register_9 (.D(multiplexer_5_out), .en(1'b1), .Q(isRet_2), .clk(clock), .clr(reset));
  Register #(.width(1)) register_10 (.D(multiplexer_6_out), .en(1'b1), .Q(isUbranch_2), .clk(clock), .clr(reset));
  Register #(.width(1)) register_11 (.D(multiplexer_1_out), .en(1'b1), .Q(isCall_2), .clk(clock), .clr(reset));
  Register #(.width(13)) register_12 (.D(multiplexer_8_out), .en(1'b1), .Q(Alusignals_2), .clk(clock), .clr(reset));
  Register #(.width(1)) register_13 (.D(multiplexer_10_out), .en(1'b1), .Q(isLd_2), .clk(clock), .clr(reset));
  Register #(.width(1)) register_14 (.D(multiplexer_3_out), .en(1'b1), .Q(isBeq_2), .clk(clock), .clr(reset));
  Register #(.width(1)) register_15 (.D(multiplexer_7_out), .en(1'b1), .Q(isWb_2), .clk(clock), .clr(reset));
endmodule

// EX-MA LATCH
module EX_MA (
  input  isSt,
  input  isLd,
  input  isBeq,
  input  isBgt,
  input  isRet,
  input  isWb,
  input  isUBranch,
  input  isCall,
  input  [31:0] PC_input,
  input  [31:0] aluResult,
  input  [31:0] op2_input,
  input  [31:0] Instruction,
  input  clock,
  input  clear,
  output isWb_2,
  output isUBranch_2,
  output isCall_2,
  output isST_2,
  output isLd_2,
  output isBeq_2,
  output isBgt_2,
  output isRet_2,
  output [31:0] Instruction_2,
  output [31:0] PC_input_2,
  output [31:0] aluResult_2,
  output [31:0] op2_input_2
);

  Register #(.width(32)) register_1 (.D(PC_input), .en(1'b1), .Q(PC_input_2), .clk(clock), .clr(clear));
  Register #(.width(32)) register_2 (.D(aluResult), .en(1'b1), .Q(aluResult_2), .clk(clock), .clr(clear));
  Register #(.width(32)) register_3 (.D(op2_input), .en(1'b1), .Q(op2_input_2), .clk(clock), .clr(clear));
  Register #(.width(32)) register_4 (.D(Instruction), .en(1'b1), .Q(Instruction_2), .clk(clock), .clr(clear));
  Register #(.width(1)) register_5 (.D(isSt), .en(1'b1), .Q(isST_2), .clk(clock), .clr(clear));
  Register #(.width(1)) register_6 (.D(isLd), .en(1'b1), .Q(isLd_2), .clk(clock), .clr(clear));
  Register #(.width(1)) register_7 (.D(isBeq), .en(1'b1), .Q(isBeq_2), .clk(clock), .clr(clear));
  Register #(.width(1)) register_8 (.D(isBgt), .en(1'b1), .Q(isBgt_2), .clk(clock), .clr(clear));
  Register #(.width(1)) register_9 (.D(isRet), .en(1'b1), .Q(isRet_2), .clk(clock), .clr(clear));
  Register #(.width(1)) register_10 (.D(isWb), .en(1'b1), .Q(isWb_2), .clk(clock), .clr(clear));
  Register #(.width(1)) register_11 (.D(isUBranch), .en(1'b1), .Q(isUBranch_2), .clk(clock), .clr(clear));
  Register #(.width(1)) register_12 (.D(isCall), .en(1'b1), .Q(isCall_2), .clk(clock), .clr(clear));
endmodule

// MA-RW LATCH
module MA_RW (
  input  isSt,
  input  isLd,
  input  isBeq,
  input  isBgt,
  input  isRet,
  input  isWb,
  input  isUBranch,
  input  isCall,
  input  [31:0] pc_input,
  input  [31:0] ldResult,
  input  [31:0] aluResult,
  input  [31:0] instruction,
  input  clock,
  input  clear,
  output [31:0] pc_o_p,
  output [31:0] IdResult_o_p,
  output [31:0] aluResult_o_p,
  output [31:0] ins_o_p,
  output isUBranch_2,
  output isCall_2,
  output isWb_2,
  output isBeq_2,
  output isBgt_2,
  output isRet_2,
  output isSt_2,
  output isLd_2
);

  Register #(.width(32)) register_1 (.D(pc_input), .en(1'b1), .Q(pc_o_p), .clk(clock), .clr(clear));
  Register #(.width(32)) register_2 (.D(ldResult), .en(1'b1), .Q(IdResult_o_p), .clk(clock), .clr(clear));
  Register #(.width(32)) register_3 (.D(aluResult), .en(1'b1), .Q(aluResult_o_p), .clk(clock), .clr(clear));
  Register #(.width(32)) register_4 (.D(instruction), .en(1'b1), .Q(ins_o_p), .clk(clock), .clr(clear));
  Register #(.width(1)) register_5 (.D(isSt), .en(1'b1), .Q(isSt_2), .clk(clock), .clr(clear));
  Register #(.width(1)) register_6 (.D(isLd), .en(1'b1), .Q(isLd_2), .clk(clock), .clr(clear));
  Register #(.width(1)) register_7 (.D(isBeq), .en(1'b1), .Q(isBeq_2), .clk(clock), .clr(clear));
  Register #(.width(1)) register_8 (.D(isBgt), .en(1'b1), .Q(isBgt_2), .clk(clock), .clr(clear));
  Register #(.width(1)) register_9 (.D(isRet), .en(1'b1), .Q(isRet_2), .clk(clock), .clr(clear));
  Register #(.width(1)) register_10 (.D(isWb), .en(1'b1), .Q(isWb_2), .clk(clock), .clr(clear));
  Register #(.width(1)) register_11 (.D(isUBranch), .en(1'b1), .Q(isUBranch_2), .clk(clock), .clr(clear));
  Register #(.width(1)) register_12 (.D(isCall), .en(1'b1), .Q(isCall_2), .clk(clock), .clr(clear));
endmodule

module forwarding_circuit (
  input  [31:0] InstA,
  input  [31:0] InstB,
  output FO_conflict,
  output SO_conflict
);

  wire and_1_out, comparator_1_eq, comparator_2_eq, isb_2_out, isb_3_out, isb_4_out, isb_out, isBeq_2_out,
       isBeq_3_out, isBeq_4_out, isBeq_out, isBgt_2_out, isBgt_3_out, isBgt_4_out, isBgt_out, isCall_2_out,
       isCall_3_out, isCall_4_out, isCall_out, iscmp_2_out, iscmp_out, ismov_out, isnot_out, isRet_2_out,
       isRet_3_out, isRet_out, isSt_2_out, isSt_3_out, isSt_out, multiplexer_5_out, nop_2_out, nop_3_out,
       nop_4_out, nop_out, not_1_out, not_2_out, not_3_out, not_4_out, not_5_out, or_1_out, or_2_out,
       or_3_out, or_4_out;
  wire [3:0] dest, dest2, src1, src2;

  and isBeq (isBeq_out, ~InstA[27], ~InstA[28], ~InstA[29], ~InstA[30], InstA[31]);  // AND_Gate
  and isBgt (isBgt_out, InstA[27], ~InstA[28], ~InstA[29], ~InstA[30], InstA[31]);  // AND_Gate
  and isb (isb_out, ~InstA[27], InstA[28], ~InstA[29], ~InstA[30], InstA[31]);  // AND_Gate
  and isCall (isCall_out, InstA[27], InstA[28], ~InstA[29], ~InstA[30], InstA[31]);  // AND_Gate
  and nop (nop_out, InstA[27], ~InstA[28], InstA[29], InstA[30], ~InstA[31]);  // AND_Gate
  and ismov (ismov_out, InstA[27], ~InstA[28], ~InstA[29], InstA[30], ~InstA[31]);  // AND_Gate
  and isnot (isnot_out, ~InstA[27], ~InstA[28], ~InstA[29], InstA[30], ~InstA[31]);  // AND_Gate
  and isRet (isRet_out, ~InstA[27], ~InstA[28], InstA[29], ~InstA[30], InstA[31]);  // AND_Gate
  and isCall_2 (isCall_2_out, InstB[27], InstB[28], ~InstB[29], ~InstB[30], InstB[31]);  // AND_Gate
  and isBeq_2 (isBeq_2_out, ~InstB[27], ~InstB[28], ~InstB[29], ~InstB[30], InstB[31]);  // AND_Gate
  and isBgt_2 (isBgt_2_out, InstB[27], ~InstB[28], ~InstB[29], ~InstB[30], InstB[31]);  // AND_Gate
  and isb_2 (isb_2_out, ~InstB[27], InstB[28], ~InstB[29], ~InstB[30], InstB[31]);  // AND_Gate
  and isSt (isSt_out, InstB[27], InstB[28], InstB[29], InstB[30], ~InstB[31]);  // AND_Gate
  and nop_2 (nop_2_out, InstB[27], ~InstB[28], InstB[29], InstB[30], ~InstB[31]);  // AND_Gate
  and isRet_2 (isRet_2_out, ~InstB[27], ~InstB[28], InstB[29], ~InstB[30], InstB[31]);  // AND_Gate
  and iscmp (iscmp_out, InstB[27], ~InstB[28], InstB[29], ~InstB[30], ~InstB[31]);  // AND_Gate
  and isCall_3 (isCall_3_out, InstB[27], InstB[28], ~InstB[29], ~InstB[30], InstB[31]);  // AND_Gate
  and isBeq_3 (isBeq_3_out, ~InstB[27], ~InstB[28], ~InstB[29], ~InstB[30], InstB[31]);  // AND_Gate
  and isBgt_3 (isBgt_3_out, InstB[27], ~InstB[28], ~InstB[29], ~InstB[30], InstB[31]);  // AND_Gate
  and isb_3 (isb_3_out, ~InstB[27], InstB[28], ~InstB[29], ~InstB[30], InstB[31]);  // AND_Gate
  and isSt_2 (isSt_2_out, InstB[27], InstB[28], InstB[29], InstB[30], ~InstB[31]);  // AND_Gate
  and nop_3 (nop_3_out, InstB[27], ~InstB[28], InstB[29], InstB[30], ~InstB[31]);  // AND_Gate
  and isRet_3 (isRet_3_out, ~InstB[27], ~InstB[28], InstB[29], ~InstB[30], InstB[31]);  // AND_Gate
  and iscmp_2 (iscmp_2_out, InstB[27], ~InstB[28], InstB[29], ~InstB[30], ~InstB[31]);  // AND_Gate
  and isBeq_4 (isBeq_4_out, ~InstA[27], ~InstA[28], ~InstA[29], ~InstA[30], InstA[31]);  // AND_Gate
  and isBgt_4 (isBgt_4_out, InstA[27], ~InstA[28], ~InstA[29], ~InstA[30], InstA[31]);  // AND_Gate
  and isb_4 (isb_4_out, ~InstA[27], InstA[28], ~InstA[29], ~InstA[30], InstA[31]);  // AND_Gate
  and isCall_4 (isCall_4_out, InstA[27], InstA[28], ~InstA[29], ~InstA[30], InstA[31]);  // AND_Gate
  and nop_4 (nop_4_out, InstA[27], ~InstA[28], InstA[29], InstA[30], ~InstA[31]);  // AND_Gate
  and isSt_3 (isSt_3_out, InstA[27], InstA[28], InstA[29], InstA[30], ~InstA[31]);  // AND_Gate
  Multiplexer #(.width(4), .enable("false")) multiplexer_1 (
    .in0(InstA[17:14]), .in1(InstA[25:22]), .out(src2), .sel(isSt_3_out));
  Multiplexer #(.width(4), .enable("false")) multiplexer_2 (
    .in0(InstB[25:22]), .in1(4'b1111), .out(dest2), .sel(isCall_3_out));
  or or_1 (or_1_out, isBeq_out, isBgt_out, isb_out, isCall_out, nop_out, ismov_out, isnot_out);
  Multiplexer #(.width(4), .enable("false")) multiplexer_3 (
    .in0(InstA[21:18]), .in1(4'b1111), .out(src1), .sel(isRet_out));
  Multiplexer #(.width(4), .enable("false")) multiplexer_4 (
    .in0(InstB[25:22]), .in1(4'b1111), .out(dest), .sel(isCall_2_out));
  not not_1 (not_1_out, isSt_3_out);
  not not_2 (not_2_out, or_1_out);
  or or_2 (or_2_out, isBeq_2_out, isBgt_2_out, isb_2_out, isSt_out, nop_2_out, isRet_2_out, iscmp_out);
  or or_3 (or_3_out, isBeq_4_out, isBgt_4_out, isb_4_out, isCall_4_out, nop_4_out);
  not not_3 (not_3_out, or_3_out);
  or or_4 (or_4_out, isBeq_3_out, isBgt_3_out, isb_3_out, isSt_2_out, nop_3_out, isRet_3_out, iscmp_2_out);
  not not_4 (not_4_out, or_2_out);
  and and_1 (and_1_out, not_1_out, InstA[26]);
  not not_5 (not_5_out, or_4_out);
  Comparator #(.width(4)) comparator_1 (.a(src1), .b(dest), .eq(comparator_1_eq));  // open: gt, lt
  Multiplexer #(.enable("false")) multiplexer_5 (.in0(1'b1), .in1(1'b0), .out(multiplexer_5_out), .sel(and_1_out));
  Comparator #(.width(4)) comparator_2 (.a(src2), .b(dest2), .eq(comparator_2_eq));  // open: gt, lt
  and and_2 (FO_conflict, not_2_out, comparator_1_eq, not_4_out);
  and and_3 (SO_conflict, not_3_out, multiplexer_5_out, comparator_2_eq, not_5_out);

  // Notes on the sheet:
  //   isImme
  //   rd
  //   rs1
  //   rs2
  //   rd
  //   rd
endmodule

// Data Forwarding
module forwarding (
  input  [31:0] MA_RW,
  input  [31:0] EX_MA,
  input  [31:0] OF_EX,
  input  [31:0] IF_OF,
  output RW__MA_op2,
  output RW__OF_op2,
  output RW__OF_op1,
  output [1:0] RWMA__EX_op1,
  output RW__EX_op2,
  output [1:0] RWMA__EX_op2
);

  wire and_1_out, forwarding_circuit_2_so_conflict;

  forwarding_circuit forwarding_circuit_1 (
    .InstA(EX_MA), .InstB(MA_RW), .SO_conflict(RW__MA_op2));  // open: FO_conflict
  and and_1 (and_1_out, ~OF_EX[31], OF_EX[30], OF_EX[29], OF_EX[28], OF_EX[27]);  // AND_Gate
  Multiplexer #(.enable("false")) multiplexer_1 (
    .in0(forwarding_circuit_2_so_conflict), .in1(1'b0), .out(RWMA__EX_op2[1]), .sel(and_1_out));
  forwarding_circuit forwarding_circuit_2 (
    .InstA(OF_EX), .FO_conflict(RWMA__EX_op1[1]), .InstB(EX_MA),
    .SO_conflict(forwarding_circuit_2_so_conflict));
  Multiplexer #(.enable("false")) multiplexer_2 (.in0(RW__EX_op2), .in1(1'b0), .out(RWMA__EX_op2[0]), .sel(and_1_out));
  forwarding_circuit forwarding_circuit_3 (
    .InstA(OF_EX), .FO_conflict(RWMA__EX_op1[0]), .InstB(MA_RW), .SO_conflict(RW__EX_op2));
  forwarding_circuit forwarding_circuit_4 (
    .InstA(IF_OF), .FO_conflict(RW__OF_op1), .InstB(MA_RW), .SO_conflict(RW__OF_op2));
endmodule

// Branch lock
module lock_branch (
  input  isBranchTaken,
  input  stall,
  output bubble
);

  or or_1 (bubble, isBranchTaken, ~stall);  // OR_Gate
endmodule

// Conflicted data check
module data_Lock (
  input  [31:0] IF_OF_Inst,
  input  [31:0] OF_EX_Inst,
  output stall
);

  wire and_1_out, and_3_out, and_4_out, comparator_1_eq, comparator_2_eq, hasSrc1, hasSrc2, isb_2_out,
       isb_out, isBeq_2_out, isBeq_out, isBgt_2_out, isBgt_out, isCall_2_out, isCall_out, iscmp_out,
       ismov_out, isnot_out, isRet_2_out, isRet_out, isSt_2_out, isSt_3_out, isSt_out, ld, nop_2_out,
       nop_out, not_1_out, not_2_out, not_3_out, or_1_out, or_2_out, or_3_out, or_4_out;
  wire [3:0] dest, src1, src2;

  and isnot (isnot_out, ~IF_OF_Inst[27], ~IF_OF_Inst[28], ~IF_OF_Inst[29], IF_OF_Inst[30], ~IF_OF_Inst[31]);  // AND_Gate
  and isRet (isRet_out, ~IF_OF_Inst[27], ~IF_OF_Inst[28], IF_OF_Inst[29], ~IF_OF_Inst[30], IF_OF_Inst[31]);  // AND_Gate
  and isSt (isSt_out, IF_OF_Inst[27], IF_OF_Inst[28], IF_OF_Inst[29], IF_OF_Inst[30], ~IF_OF_Inst[31]);  // AND_Gate
  and isSt_2 (isSt_2_out, IF_OF_Inst[27], IF_OF_Inst[28], IF_OF_Inst[29], IF_OF_Inst[30], ~IF_OF_Inst[31]);  // AND_Gate
  and isBeq (isBeq_out, ~IF_OF_Inst[27], ~IF_OF_Inst[28], ~IF_OF_Inst[29], ~IF_OF_Inst[30], IF_OF_Inst[31]);  // AND_Gate
  and isBgt (isBgt_out, IF_OF_Inst[27], ~IF_OF_Inst[28], ~IF_OF_Inst[29], ~IF_OF_Inst[30], IF_OF_Inst[31]);  // AND_Gate
  and isb (isb_out, ~IF_OF_Inst[27], IF_OF_Inst[28], ~IF_OF_Inst[29], ~IF_OF_Inst[30], IF_OF_Inst[31]);  // AND_Gate
  and isCall (isCall_out, IF_OF_Inst[27], IF_OF_Inst[28], ~IF_OF_Inst[29], ~IF_OF_Inst[30], IF_OF_Inst[31]);  // AND_Gate
  and nop (nop_out, IF_OF_Inst[27], ~IF_OF_Inst[28], IF_OF_Inst[29], IF_OF_Inst[30], ~IF_OF_Inst[31]);  // AND_Gate
  and isBeq_2 (isBeq_2_out, ~OF_EX_Inst[27], ~OF_EX_Inst[28], ~OF_EX_Inst[29], ~OF_EX_Inst[30], OF_EX_Inst[31]);  // AND_Gate
  and isBgt_2 (isBgt_2_out, OF_EX_Inst[27], ~OF_EX_Inst[28], ~OF_EX_Inst[29], ~OF_EX_Inst[30], OF_EX_Inst[31]);  // AND_Gate
  and isb_2 (isb_2_out, ~OF_EX_Inst[27], OF_EX_Inst[28], ~OF_EX_Inst[29], ~OF_EX_Inst[30], OF_EX_Inst[31]);  // AND_Gate
  and isSt_3 (isSt_3_out, OF_EX_Inst[27], OF_EX_Inst[28], OF_EX_Inst[29], OF_EX_Inst[30], ~OF_EX_Inst[31]);  // AND_Gate
  and nop_2 (nop_2_out, OF_EX_Inst[27], ~OF_EX_Inst[28], OF_EX_Inst[29], OF_EX_Inst[30], ~OF_EX_Inst[31]);  // AND_Gate
  and isRet_2 (isRet_2_out, ~OF_EX_Inst[27], ~OF_EX_Inst[28], OF_EX_Inst[29], ~OF_EX_Inst[30], OF_EX_Inst[31]);  // AND_Gate
  and iscmp (iscmp_out, OF_EX_Inst[27], ~OF_EX_Inst[28], OF_EX_Inst[29], ~OF_EX_Inst[30], ~OF_EX_Inst[31]);  // AND_Gate
  and ismov (ismov_out, IF_OF_Inst[27], ~IF_OF_Inst[28], ~IF_OF_Inst[29], IF_OF_Inst[30], ~IF_OF_Inst[31]);  // AND_Gate
  Multiplexer #(.width(4), .enable("false")) multiplexer_1 (
    .in0(IF_OF_Inst[17:14]), .in1(IF_OF_Inst[25:22]), .out(src2), .sel(isSt_out));
  Multiplexer #(.width(4), .enable("false")) multiplexer_2 (
    .in0(IF_OF_Inst[21:18]), .in1(4'b1111), .out(src1), .sel(isRet_out));
  not not_1 (not_1_out, isSt_2_out);
  and isLd (ld, ~OF_EX_Inst[27], OF_EX_Inst[28], OF_EX_Inst[29], OF_EX_Inst[30], ~OF_EX_Inst[31]);  // AND_Gate
  and isCall_2 (isCall_2_out, OF_EX_Inst[27], OF_EX_Inst[28], ~OF_EX_Inst[29], ~OF_EX_Inst[30], OF_EX_Inst[31]);  // AND_Gate
  or or_1 (or_1_out, ismov_out, isnot_out);
  or or_2 (or_2_out, isBeq_out, isBgt_out, isb_out, isCall_out, nop_out);
  Multiplexer #(.enable("false")) multiplexer_3 (.in0(1'b1), .in1(1'b0), .out(hasSrc1), .sel(or_1_out));
  and and_1 (and_1_out, not_1_out, IF_OF_Inst[26]);
  Multiplexer #(.width(4), .enable("false")) multiplexer_4 (
    .in0(OF_EX_Inst[25:22]), .in1(4'b1111), .out(dest), .sel(isCall_2_out));
  not not_2 (not_2_out, or_2_out);
  or or_3 (or_3_out, isBeq_2_out, isBgt_2_out, isb_2_out, isSt_3_out, nop_2_out, isRet_2_out, iscmp_out);
  Multiplexer #(.enable("false")) multiplexer_5 (.in0(1'b1), .in1(1'b0), .out(hasSrc2), .sel(and_1_out));
  not not_3 (not_3_out, or_3_out);
  Comparator #(.width(4)) comparator_1 (.a(src1), .b(dest), .eq(comparator_1_eq));  // open: gt, lt
  Comparator #(.width(4)) comparator_2 (.a(src2), .b(dest), .eq(comparator_2_eq));  // open: gt, lt
  and and_2 (stall, not_2_out, not_3_out, ld, or_4_out);
  and and_3 (and_3_out, hasSrc1, comparator_1_eq);
  and and_4 (and_4_out, hasSrc2, comparator_2_eq);
  or or_4 (or_4_out, and_3_out, and_4_out);

  // Notes on the sheet:
  //   isImme
  //   rs2
  //   rd
  //   rs1
  //   rd
endmodule

// data lock
module conflicted_data (
  input  [31:0] OF,
  input  [31:0] EX,
  input  [31:0] MA,
  input  [31:0] RW,
  output out_5
);

  wire data_lock_1_stall, data_lock_2_stall, data_lock_3_stall;

  data_Lock data_lock_1 (.stall(data_lock_1_stall), .IF_OF_Inst(OF), .OF_EX_Inst(EX));
  data_Lock data_lock_2 (.stall(data_lock_2_stall), .IF_OF_Inst(OF), .OF_EX_Inst(MA));
  data_Lock data_lock_3 (.stall(data_lock_3_stall), .IF_OF_Inst(OF), .OF_EX_Inst(RW));
  or or_1 (out_5, data_lock_1_stall, data_lock_2_stall, data_lock_3_stall);
endmodule
